# Fritzing sketch 2025 WRO FUTURE ENGINEER TEKBOT WEST (saved by Fritzing 0.9.3b)
breadboards: 1

parts:
  A1 = Raspberry Pi 5
  Componente1 = Motor Driver 1A Dual TB6612FNG
  M1 = Arduino NANO RP2040 CONNECT with headers
  Bat1 = battery_holder_single_18650
  Bat2 = battery_holder_single_18650
  Bat3 = battery_holder_single_18650
  Mod1 = 3S-BMS
  J1 = Basic Servo
  M2 = DC Motor
  J2 = Infrared Proximity Sensor
  J3 = Infrared Proximity Sensor
  J4 = Infrared Proximity Sensor

nets:
  5V: A1.5V, A1.Fan-5V, J1.vcc
  N1: A1.GPIO14, M1.RX
  N2: A1.GPIO15, M1.TX
  N3: A1.GPIO12, Componente1.PWMA
  N4: A1.GPIO20, Componente1.AIN1
  N5: A1.GPIO21, Componente1.AIN2
  GND: Componente1.GND, M1.GND-4, M1.GND-29, Mod1.-, J1.gnd, J2.GND, J3.GND, J4.GND
  N6: Componente1.A02, M2.pin_2
  N7: Componente1.A01, M2.pin_1
  VCC: Componente1.VCC, Componente1.STBY, M1.VIN, J2.Vcc, J3.Vcc, J4.Vcc
  N8: Componente1.VM, Mod1.+
  N9: M1.D2, J1.pulse
  N10: M1.D14, J3.Vout
  N11: M1.D15, J2.Vout
  N12: M1.D16, J4.Vout
  N13: Bat1.+#0, Mod1.0V
  N14: Bat1.+#1, Bat2.+#0, Mod1.4.2V
  N15: Bat2.+#1, Bat3.+#0, Mod1.8.4V
  N16: Bat3.+#1, Mod1.12.6V

custom parts:
  Raspberry Pi 5: The RPi5, a faster version of the awesome Raspberry Pi4B ARM Board with 40 pin gpio.
  Arduino NANO RP2040 CONNECT with headers: Meet the only connected RP2040 board. It fits the Arduino Nano form factor, making it a small board with BIG features. The brain of the board is the Raspberry Pi RP2040 silicon; a dual-core Arm Cortex M0+ running at 133MHz. It has 264KB of SRAM, and the 16MB of flash memory is off-chip to give you extra storage. But what’s really exciting is the on-board connectivity options. The hugely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
  battery_holder_single_18650: single 18650 battery holder
  3S-BMS: 3S-BMS LIPO battery charger / protection unit. Note pcb does not match the board as it will likely connect with wires, so pcb is 6 pads suitable for .1in header pins.
