# Fritzing sketch scehamtic diagram (saved by Fritzing 0.9.3b)
breadboards: 1

parts:
  A1 = Raspberry Pi 5
  M1 = Arduino NANO RP2040 CONNECT with headers
  Bat1 = battery_holder_single_18650
  Bat2 = battery_holder_single_18650
  Bat3 = battery_holder_single_18650
  Mod1 = 3S-BMS
  J1 = Basic Servo
  M2 = DC Motor
  J2 = Infrared Proximity Sensor
  J3 = Infrared Proximity Sensor
  J4 = Infrared Proximity Sensor
  S1 = H-Bridge with L298N
  S2 = Pushbutton [package="[THT]"]
  R1 = Resistor [tolerance=±5% resistance=10k package=THT]

nets:
  5V: A1.5V, A1.Fan-5V, J1.vcc
  N1: A1.GPIO14, M1.RX
  N2: A1.GPIO15, M1.TX
  N3: A1.GPIO12, S1.ENB
  N4: A1.GPIO16, S2.Pin_1, S2.Pin_2, R1.Pin_0
  N5: A1.GPIO20, S1.IN3
  N6: A1.GPIO21, S1.IN4
  GND: M1.GND-4, M1.GND-29, Mod1.-, J1.gnd, J2.GND, J3.GND, J4.GND, S1.GND, R1.Pin_1
  N7: M1.D2, J1.pulse
  N8: M1.D14, J3.Vout
  N9: M1.D15, J2.Vout
  N10: M1.D16, J4.Vout
  VCC: M1.VIN, J2.Vcc, J3.Vcc, J4.Vcc, S1.5V, S2.Pin_3, S2.Pin_4
  N11: Bat1.+#0, Mod1.0V
  N12: Bat1.+#1, Bat2.+#0, Mod1.4.2V
  N13: Bat2.+#1, Bat3.+#0, Mod1.8.4V
  N14: Bat3.+#1, Mod1.12.6V
  N15: Mod1.+, S1.12V
  N16: M2.pin_1, S1.M1-01
  N17: M2.pin_2, S1.M1-02

notes:
  We use a powerbank to power the Raspberry pi 5 8GB Ram using a USB - USB-C cable.
  We use a Microsoft LifeCam HD-3000 which is connected to the Raspberry Pi 5 8GB connected by a USB cable.
  We connect the arduino to the Raspberry Pi 5 8GB by a USB - Micro USB cable.

custom parts:
  Raspberry Pi 5: The RPi5, a faster version of the awesome Raspberry Pi4B ARM Board with 40 pin gpio.
  Arduino NANO RP2040 CONNECT with headers: Meet the only connected RP2040 board. It fits the Arduino Nano form factor, making it a small board with BIG features. The brain of the board is the Raspberry Pi RP2040 silicon; a dual-core Arm Cortex M0+ running at 133MHz. It has 264KB of SRAM, and the 16MB of flash memory is off-chip to give you extra storage. But what’s really exciting is the on-board connectivity options. The hugely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
  battery_holder_single_18650: single 18650 battery holder
  3S-BMS: 3S-BMS LIPO battery charger / protection unit. Note pcb does not match the board as it will likely connect with wires, so pcb is 6 pads suitable for .1in header pins.
  H-Bridge with L298N: h-bridge
